# Fritzing sketch experiment0 (saved by Fritzing 0.8.7b)
breadboards: 1

parts:
  Part1 = Arduino Uno (Rev3)
  R1 = Resistor [tolerance=±5% resistance=220 package=THT]
  LED1 = LED - 5mm [color="Red (633nm)" package="5 mm [THT]"]
  S2 = Round Pushbutton

nets:
  N1: Part1.D13/SCK, LED1.cathode
  N2: Part1.D7, S2.leg0
  N3: Part1.5V, S2.leg1
  N4: Part1.GND, R1.Pin_1
  N5: R1.Pin_0, LED1.anode
