# Fritzing sketch experiment2 (saved by Fritzing 0.8.7b)
breadboards: 1

parts:
  Part1 = Arduino Uno (Rev3)
  S1 = Round Pushbutton
  S2 = Round Pushbutton
  S3 = Round Pushbutton
  LED3 = LEDs [package=led10mm]

nets:
  N1: Part1.D9_PWM, S3.leg0
  N2: Part1.D10_PWM/SS, S2.leg0
  N3: Part1.D11_PWM/MOSI, S1.leg0
  N4: Part1.D3_PWM, LED3.A
  N5: Part1.5V, S1.leg1, S2.leg1, S3.leg1
  N6: Part1.GND, LED3.C
